# Fritzing sketch pull_down_taster (saved by Fritzing 0.9.10b)
breadboards: 1

parts:
  Part1 = Arduino Uno (Rev3)
  S1 = Momentary Switch [package=ksa_sealed_tac_switch]
  R1 = Resistor [tolerance=±5% resistance=220 package="2010 [SMD]"]
  LED1 = smd LED [color="Red (633nm)" package="1206 [SMD]"]
  R2 = Resistor [tolerance=±5% resistance=220 package="2010 [SMD]"]

nets:
  N1: Part1.D10_PWM/SS, R2.Pin_0
  N2: Part1.D2, S1.1, R1.Pin_1
  N3: Part1.GND, R1.Pin_0
  N4: LED1.anode, R2.Pin_1

notes:
  Pull-Down
