# Fritzing sketch schaltaufbau (saved by Fritzing 0.9.10b)
breadboards: 1

parts:
  Part1 = Arduino Uno (Rev3)
  LED1 = smd LED [color="Red (633nm)" package="1206 [SMD]"]
  R1 = Resistor [tolerance=±5% resistance=330 package="2010 [SMD]"]

nets:
  N1: Part1.GND, LED1.cathode
  N2: Part1.D5_PWM, R1.Pin_0
  N3: LED1.anode, R1.Pin_1

notes:
  330Ω oder 220Ω
  LED
